// Logisim project ex5.circ as structural Verilog: 5 circuits, main circuit rotr
module rotr (
  input  [15:0] A,
  input  [3:0] B,
  output [15:0] Out1
);

  wire not_1_out, not_2_out, not_3_out, not_4_out;
  wire [15:0] multiplexer_1_out, multiplexer_2_out, multiplexer_3_out, rot1_1_out_2, rot2_1_out_2,
       rot4_1_out_2, rot8_1_out_2;

  rot8 rot8_1 (.in_1(A), .out_2(rot8_1_out_2));
  Multiplexer #(.width(16), .enable("false")) multiplexer_1 (
    .in0(rot8_1_out_2), .in1(A), .out(multiplexer_1_out), .sel(not_1_out));
  not not_1 (not_1_out, B[3]);
  rot4 rot4_1 (.in_1(multiplexer_1_out), .out_2(rot4_1_out_2));
  Multiplexer #(.width(16), .enable("false")) multiplexer_2 (
    .in0(rot4_1_out_2), .in1(multiplexer_1_out), .out(multiplexer_2_out), .sel(not_2_out));
  not not_2 (not_2_out, B[2]);
  rot2 rot2_1 (.in_1(multiplexer_2_out), .out_2(rot2_1_out_2));
  Multiplexer #(.width(16), .enable("false")) multiplexer_3 (
    .in0(rot2_1_out_2), .in1(multiplexer_2_out), .out(multiplexer_3_out), .sel(not_3_out));
  not not_3 (not_3_out, B[1]);
  rot1 rot1_1 (.in_1(multiplexer_3_out), .out_2(rot1_1_out_2));
  Multiplexer #(.width(16), .enable("false")) multiplexer_4 (
    .in0(rot1_1_out_2), .in1(multiplexer_3_out), .out(Out1), .sel(not_4_out));
  not not_4 (not_4_out, B[0]);

  // Notes on the sheet:
  //   PUT CIRCUITRY HERE
endmodule

module rot8 (
  input  [15:0] in_1,
  output [15:0] out_2
);

  wire [15:0] rot4_1_out_2;

  rot4 rot4_1 (.in_1(in_1), .out_2(rot4_1_out_2));
  rot4 rot4_2 (.in_1(rot4_1_out_2), .out_2(out_2));

  // Notes on the sheet:
  //   PUT CIRCUITRY HERE
endmodule

module rot4 (
  input  [15:0] in_1,
  output [15:0] out_2
);

  wire [15:0] rot2_1_out_2;

  rot2 rot2_1 (.in_1(in_1), .out_2(rot2_1_out_2));
  rot2 rot2_2 (.in_1(rot2_1_out_2), .out_2(out_2));

  // Notes on the sheet:
  //   PUT CIRCUITRY HERE
endmodule

module rot2 (
  input  [15:0] in_1,
  output [15:0] out_2
);

  wire [15:0] rot1_1_out_2;

  rot1 rot1_1 (.in_1(in_1), .out_2(rot1_1_out_2));
  rot1 rot1_2 (.in_1(rot1_1_out_2), .out_2(out_2));

  // Notes on the sheet:
  //   PUT CIRCUITRY HERE
endmodule

module rot1 (
  input  [15:0] in_1,
  output [15:0] out_2
);


  assign out_2 = {in_1[14:0], in_1[15]};

  // Notes on the sheet:
  //   PUT CIRCUITRY HERE
endmodule
